# Fritzing sketch MMMv1 (saved by Fritzing 0.8.3b)
breadboards: 1

parts:
  U2 = attiny85 [package=dip]
  D1 = Diode [package=diode-1n4148]
  D2 = Diode [package=diode-1n4148]
  R1 = Resistor [tolerance=±5% resistance=1.5k package=THT]
  C1 = Electrolytic Capacitor [capacitance=0.1nF package="100 mil [THT, electrolytic]"]
  R2 = Resistor [tolerance=±5% resistance=68 package=THT]
  R3 = Resistor [tolerance=±5% resistance=68 package=THT]
  U1 = attiny85 [package=dip]
  R4 = Resistor [tolerance=±5% resistance=1M package=THT]
  J1 = Basic Force Sensing Resistor (FSR) [package=THT]
  CONN1 = USB connector [package=THT]

nets:
  N1: U2.Pin_3, R4.Pin_1, J1.pin_1
  N2: U2.Pin_4, C1.-, U1.Pin_4, J1.pin_0, CONN1.GND, CONN1.chassis5, CONN1.chassis6
  N3: U2.Pin_5, U1.Pin_2
  N4: U2.Pin_8, D1.A, R4.Pin_0, CONN1.5V
  N5: D1.C, D2.A
  N6: D2.C, R1.Pin_0, C1.+, U1.Pin_8
  N7: R1.Pin_1, R2.Pin_1, CONN1.d-
  N8: R2.Pin_0, U1.Pin_5
  N9: R3.Pin_0, U1.Pin_7
  N10: R3.Pin_1, CONN1.d+
