# Fritzing sketch MMMv1_keyboard (saved by Fritzing 0.8.3b)
breadboards: 1

parts:
  CONN1 = USB connector [package=THT]
  D1 = Diode [package=diode-1n4148]
  D2 = Diode [package=diode-1n4148]
  R1 = Resistor [tolerance=±5% resistance=1.5k package=THT]
  C1 = Electrolytic Capacitor [capacitance=0.1nF package="100 mil [THT, electrolytic]"]
  R2 = Resistor [tolerance=±5% resistance=68 package=THT]
  R3 = Resistor [tolerance=±5% resistance=68 package=THT]
  U1 = attiny85 [package=dip]

nets:
  N1: CONN1.5V, D1.A
  N2: CONN1.d-, R1.Pin_1, R2.Pin_1
  N3: CONN1.d+, R3.Pin_1
  N4: CONN1.chassis6, C1.-, U1.Pin_4
  N5: D1.C, D2.A
  N6: D2.C, R1.Pin_0, C1.+, U1.Pin_8
  N7: R2.Pin_0, U1.Pin_5
  N8: R3.Pin_0, U1.Pin_7
