# Fritzing sketch incomplete (saved by Fritzing 0.8.7b)
breadboards: 1

parts:
  U1 = attiny85 [package=dip]
  R1 = Resistor [tolerance=±5% resistance=68 package=THT]
  R2 = Resistor [tolerance=±5% resistance=68 package=THT]
  D2 = Zener Diode [part_number=1N4148 breakdown_voltage=3.6V package="Melf DO-213 AB [SMD]"]
  R3 = Resistor [tolerance=±5% resistance=220 package=THT]
  CONN1 = USB connector [package=THT]
  D3 = Zener Diode [part_number=1N4148 breakdown_voltage=3.6V package="Melf DO-213 AB [SMD]"]

nets:
  N1: U1.Pin_2, R2.Pin_0
  N2: U1.Pin_3, R1.Pin_0
  N3: U1.Pin_4, D2.anode, CONN1.5V, D3.anode
  N4: U1.Pin_8, R3.Pin_1, CONN1.GND, CONN1.chassis5, CONN1.chassis6
  N5: R1.Pin_1, D2.cathode, R3.Pin_0, CONN1.d+
  N6: R2.Pin_1, CONN1.d-, D3.cathode
