# Fritzing sketch MMMv1_input (saved by Fritzing 0.8.3b)
breadboards: 1

parts:
  CONN1 = USB connector [package=THT]
  R4 = Resistor [tolerance=±5% resistance=1M package=THT]
  J1 = Basic Force Sensing Resistor (FSR) [package=THT]
  U2 = attiny85 [package=dip]

nets:
  N1: CONN1.5V, R4.Pin_0, U2.Pin_8
  N2: CONN1.chassis6, J1.pin_0, U2.Pin_4
  N3: R4.Pin_1, J1.pin_1, U2.Pin_3
