# Fritzing sketch updated_test (saved by Fritzing 0.8.3b)
circuit board: 4.85418cm x 5.715cm
breadboards: 1

parts:
  D1 = Diode [package=diode-1n4148]
  D2 = Diode [package=diode-1n4148]
  R1 = Resistor [tolerance=±5% resistance=1.5k package=THT]
  C1 = Electrolytic Capacitor [capacitance=0.1nF package="100 mil [THT, electrolytic]"]
  R2 = Resistor [tolerance=±5% resistance=68 package=THT]
  R3 = Resistor [tolerance=±5% resistance=68 package=THT]
  U1 = attiny85 [package=dip]
  J1 = female pin header, 2 pins [form="♀ (female)"]
  usb_(gbwr) = female pin header, 2 pins [form="♀ (female)"]
  R5 = Resistor [tolerance=±5% resistance=1M package=THT]
  U2 = attiny85 [package=dip]

nets:
  N1: D1.A, J1.pin2
  N2: D1.C, D2.A
  N3: D2.C, R1.Pin_0, C1.+, U1.Pin_8, R5.Pin_0, U2.Pin_8
  N4: R1.Pin_1, R2.Pin_1, J1.pin1
  N5: C1.-, U1.Pin_4, usb_(gbwr).pin1, U2.Pin_4
  N6: R2.Pin_0, U1.Pin_5
  N7: R3.Pin_0, U1.Pin_7
  N8: R3.Pin_1, usb_(gbwr).pin2
  N9: U1.Pin_2, U2.Pin_5
  N10: R5.Pin_1, U2.Pin_3
